// Logisim project VM252.circ as structural Verilog: 5 circuits, main circuit MultiClockCycleVM252
module VM252ALU (
  input  in_1,
  input  [15:0] in_2,
  input  [15:0] in_3,
  output [15:0] out_4
);

  wire [15:0] multiplexer_1_out, negator_1_out;

  Multiplexer #(.width(16)) multiplexer_1 (.in0(in_3), .in1(negator_1_out), .out(multiplexer_1_out), .sel(in_1));
  Negator #(.width(16)) negator_1 (.in(in_3), .out(negator_1_out));
  Adder #(.width(16)) adder_1 (.a(in_2), .b(multiplexer_1_out), .out(out_4));  // open: cin, cout
endmodule

module VM252OPDecoder (
  input  [7:0] in_1,
  output out_2,
  output out_3,
  output out_4,
  output out_5,
  output out_6,
  output out_7,
  output out_8,
  output out_9,
  output out_10,
  output out_11,
  output out_12,
  output out_13,
  output out_14,
  output out_15,
  output out_16
);

  wire not_1_out, not_2_out, not_3_out, not_4_out, not_5_out, not_6_out, not_7_out, not_8_out, not_9_out,
       not_10_out, not_11_out, not_12_out, not_13_out, not_14_out, not_15_out, not_16_out, not_17_out;

  and and_1 (out_4, in_1[7], in_1[6], in_1[5], in_1[4], not_1_out, not_2_out);
  not not_1 (not_1_out, in_1[3]);
  not not_2 (not_2_out, in_1[2]);
  and and_2 (out_5, in_1[7], in_1[6], in_1[5], in_1[4], not_3_out, in_1[2]);
  not not_3 (not_3_out, in_1[3]);
  and and_3 (out_6, in_1[7], in_1[6], in_1[5], in_1[4], in_1[3], not_4_out);
  not not_4 (not_4_out, in_1[2]);
  and and_4 (out_7, in_1[7], in_1[6], in_1[5], in_1[4], in_1[3], in_1[2]);
  not not_5 (not_5_out, in_1[5]);
  not not_6 (not_6_out, in_1[6]);
  and and_5 (out_8, not_5_out, not_6_out, not_7_out);
  not not_7 (not_7_out, in_1[7]);
  not not_8 (not_8_out, in_1[6]);
  and and_6 (out_9, in_1[5], not_8_out, not_9_out);
  not not_9 (not_9_out, in_1[7]);
  not not_10 (not_10_out, in_1[5]);
  and and_7 (out_10, not_10_out, in_1[6], not_11_out);
  not not_11 (not_11_out, in_1[7]);
  and and_8 (out_11, in_1[5], in_1[6], not_12_out);
  not not_12 (not_12_out, in_1[7]);
  not not_13 (not_13_out, in_1[5]);
  not not_14 (not_14_out, in_1[6]);
  and and_9 (out_12, not_13_out, not_14_out, in_1[7]);
  not not_15 (not_15_out, in_1[6]);
  and and_10 (out_13, in_1[5], not_15_out, in_1[7]);
  not not_16 (not_16_out, in_1[5]);
  and and_11 (out_14, not_16_out, in_1[6], in_1[7]);
  not not_17 (not_17_out, in_1[4]);
  and and_12 (out_15, not_17_out, in_1[5], in_1[6], in_1[7]);
  or or_1 (out_2, out_4, out_5, out_6, out_7);
  or or_2 (out_16, out_14, out_13, out_12);
  or or_3 (out_3, out_4, out_8, out_10, out_11, out_15);
endmodule

module VM252ConditionalLU (
  input  in_1,
  input  in_2,
  input  in_3,
  input  [15:0] in_4,
  output out_5
);

  wire comparator_1_eq, comparator_1_lt, multiplexer_1_out;

  Comparator #(.width(16)) comparator_1 (
    .a({16{1'b0}}), .b(in_4), .eq(comparator_1_eq), .lt(comparator_1_lt));  // open: gt
  Multiplexer multiplexer_1 (.in0(1'b1), .in1(comparator_1_lt), .out(multiplexer_1_out), .sel(in_3));
  Multiplexer multiplexer_2 (.in0(multiplexer_1_out), .in1(comparator_1_eq), .out(out_5), .sel(in_2));
endmodule

module MultiClockCycleVM252 (
);

  wire and_1_out, and_2_out, and_3_out, and_4_out, and_5_out, clock_1_out, controlled_buffer_1_out,
       not_1_out, not_2_out, not_3_out, not_4_out, or_1_out, or_2_out, or_3_out, vm252conditionallu_1_out_5,
       vm252opdecoder_1_out_16;
  wire [1:0] rom_1_data_2;
  wire [3:0] vm252outputdecoder_1_out_2, vm252outputdecoder_1_out_3, vm252outputdecoder_1_out_4,
       vm252outputdecoder_1_out_5;
  wire [6:0] keyboard_1_data;
  wire [11:0] register_3_q;
  wire [12:0] multiplexer_2_out, register_1_q;
  wire [12:12] register_3_q_2;
  wire [13:0] vm252opdecoder_1_out_15;
  wire [14:0] rom_1_data;
  wire [15:0] bit_extender_1_out, bit_extender_2_out, bit_extender_3_out, bit_extender_4_out,
       multiplexer_1_out, multiplexer_3_out, multiplexer_4_out, multiplexer_5_out, multiplexer_6_out,
       ram_1_dout, register_2_q, register_4_q, register_5_q, vm252alu_1_out_4;
  wire [15:13] register_3_q_3;

  or or_1 (or_1_out, and_5_out, rom_1_data[12]);
  Register #(.trigger("falling"), .width(13)) register_1 (
    .D(multiplexer_1_out[12:0]), .en(or_1_out), .clk(clock_1_out), .Q(register_1_q));  // open: clr
  Multiplexer #(.select(2), .width(16)) multiplexer_1 (
    .in0(vm252alu_1_out_4), .in1(bit_extender_1_out), .in2(bit_extender_2_out), .out(multiplexer_1_out),
    .sel(rom_1_data[14:13]));  // open: in3
  assign bit_extender_1_out = {{3{register_1_q[12]}}, register_1_q};  // Bit_Extender bit_extender_1
  assign bit_extender_2_out = {{3{register_3_q_2[12]}}, {register_3_q_2[12], register_3_q}};  // Bit_Extender bit_extender_2
  Multiplexer #(.width(13)) multiplexer_2 (
    .in0(register_1_q), .in1({register_3_q_2[12], register_3_q}), .out(multiplexer_2_out),
    .sel(rom_1_data[11]));
  RAM #(.addrWidth(13), .dataWidth(16)) ram_1 (
    .addr(multiplexer_2_out), .we(rom_1_data[10]), .oe(1'b1), .clk(clock_1_out), .din(register_4_q),
    .dout(ram_1_dout));
  Register #(.trigger("falling"), .width(16)) register_2 (
    .D(ram_1_dout), .en(rom_1_data[9]), .clk(clock_1_out), .Q(register_2_q));  // open: clr
  Register #(.trigger("falling"), .width(16)) register_3 (
    .D(ram_1_dout), .en(rom_1_data[8]), .clk(clock_1_out),
    .Q({register_3_q_3, register_3_q_2[12], register_3_q}));  // open: clr
  Multiplexer #(.width(16)) multiplexer_3 (
    .in0({register_3_q_3, register_3_q_2[12], register_3_q}), .in1(bit_extender_3_out),
    .out(multiplexer_3_out), .sel(vm252opdecoder_1_out_15[2]));
  and and_1 (and_1_out, vm252opdecoder_1_out_15[13], not_1_out, vm252opdecoder_1_out_15[1]);
  not not_1 (not_1_out, vm252opdecoder_1_out_15[0]);
  Clock clock_1 (.out(clock_1_out));
  assign bit_extender_3_out = {{4{register_3_q[11]}}, register_3_q};  // Bit_Extender bit_extender_3
  assign controlled_buffer_1_out = and_1_out ? clock_1_out : 1'bz;  // Controlled_Buffer controlled_buffer_1
  Keyboard keyboard_1 (
    .clk(controlled_buffer_1_out), .re(vm252opdecoder_1_out_15[13]), .data(keyboard_1_data));  // open: clr, avail
  Multiplexer #(.select(2), .width(16)) multiplexer_4 (
    .in0(vm252alu_1_out_4), .in1(multiplexer_3_out), .in2(ram_1_dout), .in3(bit_extender_4_out),
    .out(multiplexer_4_out), .sel(rom_1_data_2));
  assign bit_extender_4_out = {{9{keyboard_1_data[6]}}, keyboard_1_data};  // Bit_Extender bit_extender_4
  VM252OPDecoder vm252opdecoder_1 (
    .in_1(register_2_q[15:8]), .out_16(vm252opdecoder_1_out_16), .out_8(vm252opdecoder_1_out_15[9]),
    .out_9(vm252opdecoder_1_out_15[8]), .out_10(vm252opdecoder_1_out_15[7]),
    .out_11(vm252opdecoder_1_out_15[6]), .out_12(vm252opdecoder_1_out_15[5]),
    .out_13(vm252opdecoder_1_out_15[4]), .out_14(vm252opdecoder_1_out_15[3]),
    .out_15(vm252opdecoder_1_out_15[2]), .out_4(vm252opdecoder_1_out_15[13]),
    .out_5(vm252opdecoder_1_out_15[12]), .out_6(vm252opdecoder_1_out_15[11]),
    .out_7(vm252opdecoder_1_out_15[10]));  // open: out_2, out_3
  Register #(.trigger("falling"), .width(16)) register_4 (
    .D(multiplexer_4_out), .en(rom_1_data[5]), .clk(clock_1_out), .Q(register_4_q));  // open: clr
  Register #(.trigger("falling"), .width(16)) register_5 (
    .D(register_4_q), .en(rom_1_data[2]), .clk(clock_1_out), .Q(register_5_q));  // open: clr
  Multiplexer #(.width(16)) multiplexer_5 (
    .in0(bit_extender_1_out), .in1(register_4_q), .out(multiplexer_5_out), .sel(rom_1_data[4]));
  Multiplexer #(.width(16)) multiplexer_6 (
    .in0(16'h1), .in1({register_3_q_3, register_3_q_2[12], register_3_q}), .out(multiplexer_6_out),
    .sel(rom_1_data[3]));
  Vm252OutputDecoder vm252outputdecoder_1 (
    .in_1(register_5_q), .out_2(vm252outputdecoder_1_out_2), .out_3(vm252outputdecoder_1_out_3),
    .out_4(vm252outputdecoder_1_out_4), .out_5(vm252outputdecoder_1_out_5));
  not not_2 (not_2_out, vm252opdecoder_1_out_15[0]);
  and and_2 (and_2_out, not_2_out, vm252opdecoder_1_out_15[1], vm252opdecoder_1_out_15[6]);
  not not_3 (not_3_out, vm252opdecoder_1_out_15[1]);
  and and_3 (and_3_out, vm252opdecoder_1_out_15[0], not_3_out, vm252opdecoder_1_out_15[6]);
  Hex_Digit_Display hex_digit_display_1 (.value(vm252outputdecoder_1_out_5));  // open: dp
  ROM #(.addrWidth(14), .dataWidth(15)) rom_1 (
    .addr(vm252opdecoder_1_out_15), .data({rom_1_data[14:8], rom_1_data_2, rom_1_data[5:0]}));
  not not_4 (not_4_out, vm252opdecoder_1_out_15[1]);
  and and_4 (and_4_out, vm252opdecoder_1_out_15[10], vm252opdecoder_1_out_15[0], not_4_out);
  or or_2 (or_2_out, and_2_out, and_3_out);
  or or_3 (or_3_out, or_2_out, and_4_out);
  Hex_Digit_Display hex_digit_display_2 (.value(vm252outputdecoder_1_out_4));  // open: dp
  Hex_Digit_Display hex_digit_display_3 (.value(vm252outputdecoder_1_out_3));  // open: dp
  VM252ALU vm252alu_1 (.in_2(multiplexer_5_out), .in_3(multiplexer_6_out), .in_1(or_3_out), .out_4(vm252alu_1_out_4));
  VM252ConditionalLU vm252conditionallu_1 (
    .in_4(register_4_q), .in_1(vm252opdecoder_1_out_15[5]), .in_2(vm252opdecoder_1_out_15[4]),
    .in_3(vm252opdecoder_1_out_15[3]), .out_5(vm252conditionallu_1_out_5));
  Hex_Digit_Display hex_digit_display_4 (.value(vm252outputdecoder_1_out_2));  // open: dp
  and and_5 (and_5_out, vm252opdecoder_1_out_16, vm252conditionallu_1_out_5);
  Register #(.trigger("falling"), .width(2)) register_6 (
    .D(rom_1_data[1:0]), .en(1'b1), .clk(clock_1_out), .Q(vm252opdecoder_1_out_15[1:0]));  // open: clr

  // Notes on the sheet:
  //   PCSource
  //   PC
  //   I or D
  //   Memory
  //   IR
  //   MDR
  //   Clock
  //   SET op
  //   INPUT
  //   ACCsrc
  //   (Poke the keyboard with poke symbol to use and start typing)
  //   ( Only reads one ASCII character and consumes it from the 
  //   buffer during a INPUT instruction  )
  //   ACC
  //   OUTPUT
  //   ALUSrcA
  //   ALUSrcB
  //   OUTPUT DISPLAY
  //   contents of rom_1 (hex, n*v repeats v):
  //   5*0 62 1301 0 0 4002 1301 6*0 4002 1301 14*0 4002 1301 30*0 902 3b 1301 61*0 902 3b 1301 125*0 c02
  //   1301 253*0 1301 8a2 1301 510*0 1002 1301 1022*0 1301 2047*0 6 1301 4094*0 e2 1301
  //   ALU
  //   Conditional LU
  //   Control Unit
  //   TO HANDLE STOP INSTRUCTION
  //   Current Clock Cycle
endmodule

module Vm252OutputDecoder (
  input  [15:0] in_1,
  output [3:0] out_2,
  output [3:0] out_3,
  output [3:0] out_4,
  output [3:0] out_5
);


  assign out_2 = in_1[3:0];
  assign out_3 = in_1[7:4];
  assign out_4 = in_1[11:8];
  assign out_5 = in_1[15:12];
endmodule
